# Fritzing sketch pcb (saved by Fritzing 0.9.4)
circuit board: 8.46667cm x 5.64444cm
breadboards: 1

parts:
  Composant3 = BATE Arduino Pro Mini
  Q1 = Basic FET P-Channel [package="TO220 [THT]"]
  R1 = Resistor [tolerance=±5% resistance=220 package=THT]
  M1 = DC Motor
  S1 = Pushbutton [package="[THT]"]
  R1_220_Ohm = Resistor [tolerance=±5% resistance=220 package=THT]
  Composant6 = Tiny RTC - DS1307 Breakout Board
  R2 = Resistor [tolerance=±5% resistance=10k package=THT]
  VCC3 = Battery block 9V

nets:
  VCC: Composant3.VCC, S1.Pin_1, S1.Pin_2, Composant6.VCC, R2.Pin_0
  GND: Composant3.GND, Q1.source, R1_220_Ohm.Pin_0, Composant6.GND, VCC3.-
  N1: Composant3.A4, Composant6.DS
  N2: Composant3.A5, Composant6.SCL
  N3: Composant3.A3, S1.Pin_3, S1.Pin_4, R1_220_Ohm.Pin_1
  N4: Composant3.D7, R1.Pin_0
  N5: Composant3.D3_PWM, Composant6.SQ, R2.Pin_1
  N6: Q1.gate, R1.Pin_1
  N7: Q1.drain, M1.pin_2
  N8: M1.pin_1, VCC3.+

custom parts:
  Tiny RTC - DS1307 Breakout Board: The Tiny RTC is a breakout board for the Dallas Semiconductor/Maxim Integrated DS1307 real-time clock. The DS1307 counts seconds, minutes, hours, date of the month, month, day of the week, and year (with compensation for leap-years). The breakout board also has space for a DS18B20 digital thermometer.
